// Logisim project Game.circ as structural Verilog
module main (
  input  in_1
);

  wire ResetBar_out;
  wire [31:0] barhandler_1_output;

  Button L (.out(in_1));
  BarHandler barhandler_1 (.reset(ResetBar_out), .R(in_1), .L(in_1), .\output (barhandler_1_output));
  Button ResetBar (.out(ResetBar_out));
  DotMatrix #(.inputtype("row"), .matrixcols(32), .matrixrows(32), .dotshape("circle")) dotmatrix_1 (.row31(barhandler_1_output));  // open: row0, row1, row2, row3, row4, row5, row6, row7, row8, row9, row10, row11, row12, row13, row14, row15, row16, row17, row18, row19, row20, row21, row22, row23, row24, row25, row26, row27, row28, row29, row30
  // Probe on barhandler_1_output
endmodule

module BarHandler (
  input  reset,
  input  R,
  input  L,
  output [31:0] \output 
);

  wire clock, L_t, Left, R_t, Reset_t, reset_t_t, Right, update;
  wire [31:0] divider_1_out, multiplexer_1_out, multiplier_1_out, register_1_q;

  Clock clock_1 (.out(clock));
  or or_1 (R_t, R, Right);
  or or_2 (L_t, L, Left);
  or or_3 (reset_t_t, reset, Reset_t);
  or or_4 (update, R_t, L_t, reset_t_t);
  Multiplexer #(.width(32)) multiplexer_1 (
    .in0(\output ), .in1(32'h38000), .out(multiplexer_1_out), .sel(reset_t_t));  // open: en
  Register #(.width(32)) register_1 (.D(multiplexer_1_out), .en(update), .Q(register_1_q), .clk(clock));  // open: clr
  DotMatrix #(.inputtype("row"), .matrixcols(32), .matrixrows(2)) dotmatrix_1 (.row1(\output ));  // open: row0
  // Probe on register_1_q
  Button button_1 (.out(Right));
  Multiplier #(.width(32)) multiplier_1 (.a(register_1_q), .b(32'h2), .out(multiplier_1_out));  // open: cin, cout
  Divider #(.width(32)) divider_1 (.a(register_1_q), .b(32'h2), .out(divider_1_out));  // open: upper, rem
  Button button_2 (.out(Left));
  Button button_3 (.out(Reset_t));
  Multiplexer #(.width(32)) multiplexer_2 (
    .in0(multiplier_1_out), .in1(divider_1_out), .out(\output ), .sel(R_t));  // open: en

  // Other names for the same wires on the sheet: out[31:0] = \output 
endmodule

module ColisionHandler (
  input  [31:0] in_1,
  input  [31:0] in_2,
  input  in_3
);

  wire comparator_1_eq, comparator_2_eq, comparator_3_eq, comparator_4_eq;
  wire [1:0] varcolision;
  wire [31:0] multiplexer_1_out, multiplexer_4_out, multiplexer_5_out, multiplier_1_out, sal1;

  Comparator #(.width(32)) comparator_1 (.a(in_2), .b(32'hc0000000), .eq(comparator_1_eq));  // open: gt, lt
  Multiplexer #(.width(32)) multiplexer_1 (
    .in0(32'hc0000001), .in1(32'he0000000), .out(multiplexer_1_out), .sel(in_3));  // open: en
  Comparator #(.width(32)) comparator_2 (.a(in_2), .b(sal1), .eq(comparator_2_eq));  // open: gt, lt
  Multiplexer #(.width(32)) multiplexer_2 (
    .in0(in_2), .in1(multiplexer_1_out), .out(sal1), .sel(comparator_1_eq));  // open: en
  Multiplexer #(.width(2)) multiplexer_3 (.in0(2'b00), .out(varcolision), .sel(comparator_2_eq));  // open: in1, en
  Multiplexer #(.select(2), .width(32)) multiplexer_4 (
    .in0(sal1), .out(multiplexer_4_out), .sel(varcolision));  // open: in1, in2, in3, en
  // Probe on multiplexer_4_out
  Comparator #(.width(32)) comparator_3 (.a(in_2), .b(32'hc0000000), .eq(comparator_3_eq));  // open: gt, lt
  Multiplexer #(.width(32)) multiplexer_5 (
    .in0(32'hc0000001), .in1(32'he0000000), .out(multiplexer_5_out), .sel(in_3));  // open: en
  // Probe on in_1
  Comparator #(.width(32)) comparator_4 (.a(in_2), .b(sal1), .eq(comparator_4_eq));  // open: gt, lt
  Multiplexer #(.width(32)) multiplexer_6 (
    .in0(in_2), .in1(multiplexer_5_out), .out(sal1), .sel(comparator_3_eq));  // open: en
  Multiplier #(.width(32)) multiplier_1 (.a(in_2), .b(32'h2), .out(multiplier_1_out));  // open: cin, cout
  Multiplexer #(.width(2)) multiplexer_7 (.in0(2'b00), .out(varcolision), .sel(comparator_4_eq));  // open: in1, en
  // Probe on multiplier_1_out

  // Other names for the same wires on the sheet: colisioninput[31:0] = in_2; tr = in_3
endmodule
